// Logisim project 25CSB1A21_Aryan_COA.circ as structural Verilog: 13 circuits, main circuit main
module main (
  input  D1,
  input  D2,
  input  D3,
  input  D4,
  input  Write,
  input  Read,
  input  Clk,
  input  InjectEn_A,
  input  in_9,
  input  in_10,
  input  in_11,
  input  in_12,
  input  in_13,
  input  in_14,
  input  in_15,
  input  Reset
);

  wire and_1_out, and_2_out, and_3_out, and_4_out, and_5_out, and_6_out, and_7_out, bitflip_8_1_out_13,
       bitflip_8_1_out_14, bitflip_8_1_out_15, bitflip_8_1_out_16, bitflip_8_1_out_17, bitflip_8_1_out_18,
       bitflip_8_1_out_19, bitflip_8_1_out_20, data_extract_4_1_out_9, data_extract_4_1_out_10,
       data_extract_4_1_out_11, data_extract_4_1_out_12, error_inject_8_1_out_13, error_inject_8_1_out_14,
       error_inject_8_1_out_15, error_inject_8_1_out_16, error_inject_8_1_out_17, error_inject_8_1_out_18,
       error_inject_8_1_out_19, error_inject_8_1_out_20, error_inject_8_2_out_13, error_inject_8_2_out_14,
       error_inject_8_2_out_15, error_inject_8_2_out_16, error_inject_8_2_out_17, error_inject_8_2_out_18,
       error_inject_8_2_out_19, error_inject_8_2_out_20, hamming_encode_4to8_1_r1, hamming_encode_4to8_1_r2,
       hamming_encode_4to8_1_r3, hamming_encode_4to8_1_r4, hamming_encode_4to8_1_r5,
       hamming_encode_4to8_1_r6, hamming_encode_4to8_1_r7, hamming_encode_4to8_1_r8, hamming_syndrome_8_1_c,
       hamming_syndrome_8_1_s1, hamming_syndrome_8_1_s2, hamming_syndrome_8_1_s4, mem_cell_8_1_q1,
       mem_cell_8_1_q2, mem_cell_8_1_q3, mem_cell_8_1_q4, mem_cell_8_1_q5, mem_cell_8_1_q6, mem_cell_8_1_q7,
       mem_cell_8_1_q8, not_1_out, secded_classify_1_doubleerr, secded_classify_1_noerr,
       secded_classify_1_singleerr;
  wire [3:0] DetectCounter_q, FixCounter_q, ReadCounter_q, UncorrectableCounter_q;

  Hamming_Encode_4to8 hamming_encode_4to8_1 (
    .D1(D1), .D2(D2), .D3(D3), .D4(D4), .R1(hamming_encode_4to8_1_r1), .R2(hamming_encode_4to8_1_r2),
    .R3(hamming_encode_4to8_1_r3), .R4(hamming_encode_4to8_1_r4), .R5(hamming_encode_4to8_1_r5),
    .R6(hamming_encode_4to8_1_r6), .R7(hamming_encode_4to8_1_r7), .R8(hamming_encode_4to8_1_r8));
  Mem_Cell_8 mem_cell_8_1 (
    .D_in1(hamming_encode_4to8_1_r1), .D_in2(hamming_encode_4to8_1_r2), .D_in3(hamming_encode_4to8_1_r3),
    .D_in4(hamming_encode_4to8_1_r4), .D_in5(hamming_encode_4to8_1_r5), .D_in6(hamming_encode_4to8_1_r6),
    .D_in7(hamming_encode_4to8_1_r7), .D_in8(hamming_encode_4to8_1_r8), .Clk(Clk), .WriteEn(Write),
    .Q1(mem_cell_8_1_q1), .Q2(mem_cell_8_1_q2), .Q3(mem_cell_8_1_q3), .Q4(mem_cell_8_1_q4),
    .Q5(mem_cell_8_1_q5), .Q6(mem_cell_8_1_q6), .Q7(mem_cell_8_1_q7), .Q8(mem_cell_8_1_q8));
  not not_1 (not_1_out, secded_classify_1_noerr);
  and and_1 (and_1_out, Read, secded_classify_1_singleerr);
  and and_2 (and_2_out, not_1_out, Read);
  and and_3 (and_3_out, secded_classify_1_doubleerr, Read);
  Counter #(.max('hf), .width(4)) ReadCounter (
    .clr(Reset), .load(1'b0), .up(1'b1), .count(Read), .clk(Clk), .Q(ReadCounter_q));  // open: D, carry
  Counter #(.max('hf), .width(4)) DetectCounter (
    .clr(Reset), .load(1'b0), .up(1'b1), .count(and_2_out), .clk(Clk), .Q(DetectCounter_q));  // open: D, carry
  Counter #(.max('hf), .width(4)) FixCounter (
    .clr(Reset), .load(1'b0), .up(1'b1), .count(and_1_out), .clk(Clk), .Q(FixCounter_q));  // open: D, carry
  Counter #(.max('hf), .width(4)) UncorrectableCounter (
    .clr(Reset), .load(1'b0), .up(1'b1), .count(and_3_out), .clk(Clk), .Q(UncorrectableCounter_q));  // open: D, carry
  Error_Inject_8 error_inject_8_1 (
    .R1(mem_cell_8_1_q1), .R2(mem_cell_8_1_q2), .R3(mem_cell_8_1_q3), .R4(mem_cell_8_1_q4),
    .R5(mem_cell_8_1_q5), .R6(mem_cell_8_1_q6), .R7(mem_cell_8_1_q7), .R8(mem_cell_8_1_q8),
    .InjectEn(InjectEn_A), .InjectPos0(in_9), .InjectPos1(in_10), .InjectPos2(in_11),
    .out_13(error_inject_8_1_out_13), .out_14(error_inject_8_1_out_14), .out_15(error_inject_8_1_out_15),
    .out_16(error_inject_8_1_out_16), .out_17(error_inject_8_1_out_17), .out_18(error_inject_8_1_out_18),
    .out_19(error_inject_8_1_out_19), .out_20(error_inject_8_1_out_20));
  Hex_Digit_Display hex_digit_display_1 (.value(ReadCounter_q));  // open: dp
  Hex_Digit_Display hex_digit_display_2 (.value(DetectCounter_q));  // open: dp
  Hex_Digit_Display hex_digit_display_3 (.value(FixCounter_q));  // open: dp
  Hex_Digit_Display hex_digit_display_4 (.value(UncorrectableCounter_q));  // open: dp
  Error_Inject_8 error_inject_8_2 (
    .R1(error_inject_8_1_out_13), .R2(error_inject_8_1_out_14), .R3(error_inject_8_1_out_15),
    .R4(error_inject_8_1_out_16), .R5(error_inject_8_1_out_17), .R6(error_inject_8_1_out_18),
    .R7(error_inject_8_1_out_19), .R8(error_inject_8_1_out_20), .InjectEn(in_12), .InjectPos0(in_13),
    .InjectPos1(in_14), .InjectPos2(in_15), .out_13(error_inject_8_2_out_13),
    .out_14(error_inject_8_2_out_14), .out_15(error_inject_8_2_out_15), .out_16(error_inject_8_2_out_16),
    .out_17(error_inject_8_2_out_17), .out_18(error_inject_8_2_out_18), .out_19(error_inject_8_2_out_19),
    .out_20(error_inject_8_2_out_20));
  Hamming_Syndrome_8 hamming_syndrome_8_1 (
    .R1(error_inject_8_2_out_13), .R2(error_inject_8_2_out_14), .R3(error_inject_8_2_out_15),
    .R4(error_inject_8_2_out_16), .R5(error_inject_8_2_out_17), .R6(error_inject_8_2_out_18),
    .R7(error_inject_8_2_out_19), .R8(error_inject_8_2_out_20), .S1(hamming_syndrome_8_1_s1),
    .S2(hamming_syndrome_8_1_s2), .S4(hamming_syndrome_8_1_s4), .C(hamming_syndrome_8_1_c));
  BitFlip_8 bitflip_8_1 (
    .R1(error_inject_8_2_out_13), .R2(error_inject_8_2_out_14), .R3(error_inject_8_2_out_15),
    .R4(error_inject_8_2_out_16), .R5(error_inject_8_2_out_17), .R6(error_inject_8_2_out_18),
    .R7(error_inject_8_2_out_19), .R8(error_inject_8_2_out_20), .S1(hamming_syndrome_8_1_s1),
    .S2(hamming_syndrome_8_1_s2), .S4(hamming_syndrome_8_1_s4), .C(hamming_syndrome_8_1_c),
    .out_13(bitflip_8_1_out_13), .out_14(bitflip_8_1_out_14), .out_15(bitflip_8_1_out_15),
    .out_16(bitflip_8_1_out_16), .out_17(bitflip_8_1_out_17), .out_18(bitflip_8_1_out_18),
    .out_19(bitflip_8_1_out_19), .out_20(bitflip_8_1_out_20));
  SECDED_Classify secded_classify_1 (
    .S1(hamming_syndrome_8_1_s1), .S2(hamming_syndrome_8_1_s2), .S4(hamming_syndrome_8_1_s4),
    .C(hamming_syndrome_8_1_c), .noErr(secded_classify_1_noerr), .singleErr(secded_classify_1_singleerr),
    .doubleErr(secded_classify_1_doubleerr));
  LED led_1 (.in(secded_classify_1_noerr));
  LED led_2 (.in(secded_classify_1_singleerr));
  LED led_3 (.in(secded_classify_1_doubleerr));
  Data_Extract_4 data_extract_4_1 (
    .in_1(bitflip_8_1_out_13), .in_2(bitflip_8_1_out_14), .in_3(bitflip_8_1_out_15),
    .in_4(bitflip_8_1_out_16), .in_5(bitflip_8_1_out_17), .in_6(bitflip_8_1_out_18),
    .in_7(bitflip_8_1_out_19), .in_8(bitflip_8_1_out_20), .out_9(data_extract_4_1_out_9),
    .out_10(data_extract_4_1_out_10), .out_11(data_extract_4_1_out_11), .out_12(data_extract_4_1_out_12));
  and and_4 (and_4_out, Read, data_extract_4_1_out_9);
  and and_5 (and_5_out, Read, data_extract_4_1_out_10);
  and and_6 (and_6_out, Read, data_extract_4_1_out_11);
  and and_7 (and_7_out, Read, data_extract_4_1_out_12);
  LED led_4 (.in(and_4_out));
  LED led_5 (.in(and_5_out));
  LED led_6 (.in(and_6_out));
  LED led_7 (.in(and_7_out));

  // Other names for the same wires on the sheet: r = Read

  // Notes on the sheet:
  //   InjectPos0_A
  //   InjectPos1_A
  //   InjectPos2_A
  //   InjectPos0_B
  //   InjectPos1_B
  //   InjectPos2_B
  //   InjectEn_B
  //   Fault Tolerant Memory System
  //   Total Number of Reads
  //   Reads Where an Error was Detected
  //   Reads with a double error
  //   Reads where a single bit error was corrected
  //   noErr
  //   singleErr
  //   DoubleErr
endmodule

module Hamming_Encode_4to8 (
  input  D1,
  input  D2,
  input  D3,
  input  D4,
  output R1,
  output R2,
  output R3,
  output R4,
  output R5,
  output R6,
  output R7,
  output R8
);

  wire n7486_1_pin3, n7486_1_pin11, n7486_2_pin1, n7486_2_pin3, n7486_2_pin8, n7486_2_pin11, n7486_3_pin3,
       n7486_3_pin11;

  _7486 #(.ShowInternalStructure("true")) u_7486_1 (
    .pin1(D1), .pin2(D3), .pin3(n7486_1_pin3), .pin4(n7486_1_pin3), .pin5(D4), .pin6(R2), .pin13(D1),
    .pin12(D2), .pin11(n7486_1_pin11), .pin10(n7486_1_pin11), .pin9(D4), .pin8(R1));
  _7486 #(.ShowInternalStructure("true")) u_7486_2 (
    .pin1(n7486_2_pin1), .pin2(D3), .pin3(n7486_2_pin3), .pin4(n7486_2_pin3), .pin5(D4), .pin6(R8),
    .pin13(R1), .pin12(R2), .pin11(n7486_2_pin11), .pin10(n7486_2_pin11), .pin9(D1), .pin8(n7486_2_pin8));
  _7486 #(.ShowInternalStructure("true")) u_7486_3 (
    .pin1(n7486_2_pin8), .pin2(R4), .pin3(n7486_3_pin3), .pin4(n7486_3_pin3), .pin5(D2), .pin6(n7486_2_pin1),
    .pin13(D2), .pin12(D3), .pin11(n7486_3_pin11), .pin10(n7486_3_pin11), .pin9(D4), .pin8(R4));

  assign R3 = D1;
  assign R5 = D2;
  assign R6 = D3;
  assign R7 = D4;
endmodule

module Hamming_Syndrome_8 (
  input  R1,
  input  R2,
  input  R3,
  input  R4,
  input  R5,
  input  R6,
  input  R7,
  input  R8,
  output S1,
  output S2,
  output S4,
  output C
);

  wire n7486_1_pin3, n7486_1_pin6, n7486_1_pin11, n7486_2_pin3, n7486_2_pin6, n7486_2_pin11, n7486_3_pin2,
       n7486_3_pin5, n7486_3_pin8, n7486_4_pin2, n7486_4_pin4, n7486_4_pin11;

  _7486 #(.ShowInternalStructure("true")) u_7486_1 (
    .pin1(R5), .pin2(R7), .pin3(n7486_1_pin3), .pin4(R2), .pin5(R3), .pin6(n7486_1_pin6), .pin13(R1),
    .pin12(R3), .pin11(n7486_1_pin11), .pin10(n7486_1_pin11), .pin9(n7486_1_pin3), .pin8(S1));
  _7486 #(.ShowInternalStructure("true")) u_7486_2 (
    .pin1(R4), .pin2(R5), .pin3(n7486_2_pin3), .pin4(R6), .pin5(R7), .pin6(n7486_2_pin6), .pin13(R6),
    .pin12(R7), .pin11(n7486_2_pin11), .pin10(n7486_2_pin11), .pin9(n7486_1_pin6), .pin8(S2));
  _7486 #(.ShowInternalStructure("true")) u_7486_3 (
    .pin1(R8), .pin2(n7486_3_pin2), .pin3(C), .pin4(R7), .pin5(n7486_3_pin5), .pin6(n7486_3_pin2),
    .pin13(n7486_2_pin3), .pin12(n7486_2_pin6), .pin11(S4), .pin10(R1), .pin9(R2), .pin8(n7486_3_pin8));
  _7486 #(.ShowInternalStructure("true")) u_7486_4 (
    .pin1(R6), .pin2(n7486_4_pin2), .pin3(n7486_3_pin5), .pin4(n7486_4_pin4), .pin5(R5), .pin6(n7486_4_pin2),
    .pin13(n7486_3_pin8), .pin12(R3), .pin11(n7486_4_pin11), .pin10(n7486_4_pin11), .pin9(R4),
    .pin8(n7486_4_pin4));

  // Notes on the sheet:
  //   Hamming_Syndrome_8
endmodule

module SECDED_Classify (
  input  S1,
  input  S2,
  input  S4,
  input  C,
  output noErr,
  output singleErr,
  output doubleErr
);

  wire n7432_1_pin8, n7432_1_pin11, not_1_out, not_2_out;

  _7432 #(.ShowInternalStructure("true")) u_7432_1 (
    .pin13(S1), .pin12(S2), .pin11(n7432_1_pin11), .pin10(n7432_1_pin11), .pin9(S4), .pin8(n7432_1_pin8));  // open: pin1, pin2, pin3, pin4, pin5, pin6
  not not_1 (not_1_out, C);
  not not_2 (not_2_out, n7432_1_pin8);
  and and_1 (noErr, not_2_out, not_1_out);
  and and_2 (doubleErr, n7432_1_pin8, not_1_out);

  assign singleErr = C;

  // Notes on the sheet:
  //   SECDED_Classify
endmodule

module Step2_Test (
  input  D1,
  input  D2,
  input  D3,
  input  D4,
  input  in_5,
  input  in_6,
  input  in_7,
  input  in_8,
  input  in_9,
  input  in_10,
  input  in_11,
  input  in_12,
  output out_13,
  output out_14,
  output out_15
);

  wire hamming_syndrome_8_1_c, hamming_syndrome_8_1_s1, hamming_syndrome_8_1_s2, hamming_syndrome_8_1_s4,
       n7486_1_pin3, n7486_1_pin6, n7486_1_pin8, n7486_1_pin11, n7486_2_pin3, n7486_2_pin6, n7486_2_pin8,
       n7486_2_pin11, R1, R2, R3, R4, R5, R6, R7, R8;

  _7486 #(.ShowInternalStructure("true")) u_7486_1 (
    .pin1(R3), .pin2(in_7), .pin3(n7486_1_pin3), .pin4(R4), .pin5(in_8), .pin6(n7486_1_pin6), .pin13(R1),
    .pin12(in_5), .pin11(n7486_1_pin11), .pin10(R2), .pin9(in_6), .pin8(n7486_1_pin8));
  Hamming_Encode_4to8 hamming_encode_4to8_1 (
    .D1(D1), .D2(D2), .D3(D3), .D4(D4), .R1(R1), .R2(R2), .R3(R3), .R4(R4), .R5(R5), .R6(R6), .R7(R7), .R8(R8));
  _7486 #(.ShowInternalStructure("true")) u_7486_2 (
    .pin1(R5), .pin2(in_9), .pin3(n7486_2_pin3), .pin4(R6), .pin5(in_10), .pin6(n7486_2_pin6), .pin13(R7),
    .pin12(in_11), .pin11(n7486_2_pin11), .pin10(R8), .pin9(in_12), .pin8(n7486_2_pin8));
  Hamming_Syndrome_8 hamming_syndrome_8_1 (
    .R1(n7486_1_pin11), .R2(n7486_1_pin8), .R3(n7486_1_pin3), .R4(n7486_1_pin6), .R5(n7486_2_pin3),
    .R6(n7486_2_pin6), .R7(n7486_2_pin11), .R8(n7486_2_pin8), .S1(hamming_syndrome_8_1_s1),
    .S2(hamming_syndrome_8_1_s2), .S4(hamming_syndrome_8_1_s4), .C(hamming_syndrome_8_1_c));
  SECDED_Classify secded_classify_1 (
    .S1(hamming_syndrome_8_1_s1), .S2(hamming_syndrome_8_1_s2), .S4(hamming_syndrome_8_1_s4),
    .C(hamming_syndrome_8_1_c), .noErr(out_13), .singleErr(out_14), .doubleErr(out_15));

  // Notes on the sheet:
  //   I1
  //   I2
  //   I3
  //   I4
  //   I5
  //   I6
  //   I7
  //   I8
endmodule

module BitFlip_8 (
  input  R1,
  input  R2,
  input  R3,
  input  R4,
  input  R5,
  input  R6,
  input  R7,
  input  R8,
  input  S1,
  input  S2,
  input  S4,
  input  C,
  output out_13,
  output out_14,
  output out_15,
  output out_16,
  output out_17,
  output out_18,
  output out_19,
  output out_20
);

  wire and_1_out, and_2_out, Flip1_out, Flip2_out, Flip3_out, Flip4_out, Flip5_out, Flip6_out, Flip7_out,
       Flip8_out, n74138_1_pin4, n74138_1_pin5, n74138_1_pin6, n74138_1_pin7, n74138_1_pin9, n74138_1_pin10,
       n74138_1_pin11, n74138_1_pin12, n74138_1_pin13, n74138_1_pin14, not_1_out, not_2_out, not_3_out,
       not_4_out, not_5_out, not_6_out, not_7_out, not_8_out, not_9_out, not_10_out;

  not not_1 (not_1_out, S1);
  not not_2 (not_2_out, S1);
  not not_3 (not_3_out, n74138_1_pin14);
  _74138 #(.ShowInternalStructure("true")) u_74138_1 (
    .pin1(S1), .pin2(S2), .pin3(S4), .pin4(n74138_1_pin4), .pin5(n74138_1_pin5), .pin6(n74138_1_pin6),
    .pin7(n74138_1_pin7), .pin14(n74138_1_pin14), .pin13(n74138_1_pin13), .pin12(n74138_1_pin12),
    .pin11(n74138_1_pin11), .pin10(n74138_1_pin10), .pin9(n74138_1_pin9));  // open: pin15
  not not_4 (not_4_out, n74138_1_pin13);
  not not_5 (not_5_out, n74138_1_pin12);
  not not_6 (not_6_out, n74138_1_pin11);
  not not_7 (not_7_out, n74138_1_pin10);
  not not_8 (not_8_out, n74138_1_pin7);
  not not_9 (not_9_out, S4);
  not not_10 (not_10_out, n74138_1_pin9);
  and and_1 (and_1_out, not_1_out, not_2_out);
  and and_2 (and_2_out, not_9_out, C);
  and Flip1 (Flip1_out, not_3_out, C);
  and Flip2 (Flip2_out, not_4_out, C);
  and Flip3 (Flip3_out, not_5_out, C);
  and Flip4 (Flip4_out, not_6_out, C);
  and Flip5 (Flip5_out, not_7_out, C);
  and Flip6 (Flip6_out, not_10_out, C);
  and Flip7 (Flip7_out, not_8_out, C);
  and Flip8 (Flip8_out, and_1_out, and_2_out);
  xor u_r1 (out_13, R1, Flip1_out);
  xor u_r2 (out_14, R2, Flip2_out);
  xor u_r3 (out_15, R3, Flip3_out);
  xor u_r4 (out_16, R4, Flip4_out);
  xor u_r5 (out_17, R5, Flip5_out);
  xor u_r6 (out_18, R6, Flip6_out);
  xor u_r7 (out_19, R7, Flip7_out);
  xor u_r8 (out_20, R8, Flip8_out);
  // also tied to GND on the sheet: {n74138_1_pin4, n74138_1_pin5}
  // also tied to VCC on the sheet: n74138_1_pin6

  // Notes on the sheet:
  //   BitFlip_8
endmodule

module Data_Extract_4 (
  input  in_1,
  input  in_2,
  input  in_3,
  input  in_4,
  input  in_5,
  input  in_6,
  input  in_7,
  input  in_8,
  output out_9,
  output out_10,
  output out_11,
  output out_12
);


  assign out_9 = in_3;
  assign out_10 = in_5;
  assign out_11 = in_6;
  assign out_12 = in_7;

  // Notes on the sheet:
  //   Data Extract
endmodule

module Step3_Test (
  input  D1,
  input  D2,
  input  D3,
  input  D4,
  input  in_5,
  input  in_6,
  input  in_7,
  input  in_8,
  input  in_9,
  input  in_10,
  input  in_11,
  input  in_12,
  output out_13,
  output out_14,
  output out_15
);

  wire bitflip_8_1_out_13, bitflip_8_1_out_14, bitflip_8_1_out_15, bitflip_8_1_out_16, bitflip_8_1_out_17,
       bitflip_8_1_out_18, bitflip_8_1_out_19, bitflip_8_1_out_20, data_extract_4_1_out_9,
       data_extract_4_1_out_10, data_extract_4_1_out_11, data_extract_4_1_out_12, hamming_syndrome_8_1_c,
       hamming_syndrome_8_1_s1, hamming_syndrome_8_1_s2, hamming_syndrome_8_1_s4, n7486_1_pin3, n7486_1_pin6,
       n7486_1_pin8, n7486_1_pin11, n7486_2_pin3, n7486_2_pin6, n7486_2_pin8, n7486_2_pin11, R1, R2, R3, R4,
       R5, R6, R7, R8;

  _7486 #(.ShowInternalStructure("true")) u_7486_1 (
    .pin1(R3), .pin2(in_7), .pin3(n7486_1_pin3), .pin4(R4), .pin5(in_8), .pin6(n7486_1_pin6), .pin13(R1),
    .pin12(in_5), .pin11(n7486_1_pin11), .pin10(R2), .pin9(in_6), .pin8(n7486_1_pin8));
  Hamming_Encode_4to8 hamming_encode_4to8_1 (
    .D1(D1), .D2(D2), .D3(D3), .D4(D4), .R1(R1), .R2(R2), .R3(R3), .R4(R4), .R5(R5), .R6(R6), .R7(R7), .R8(R8));
  _7486 #(.ShowInternalStructure("true")) u_7486_2 (
    .pin1(R5), .pin2(in_9), .pin3(n7486_2_pin3), .pin4(R6), .pin5(in_10), .pin6(n7486_2_pin6), .pin13(R7),
    .pin12(in_11), .pin11(n7486_2_pin11), .pin10(R8), .pin9(in_12), .pin8(n7486_2_pin8));
  BitFlip_8 bitflip_8_1 (
    .R1(n7486_1_pin11), .R2(n7486_1_pin8), .R3(n7486_1_pin3), .R4(n7486_1_pin6), .R5(n7486_2_pin3),
    .R6(n7486_2_pin6), .R7(n7486_2_pin11), .R8(n7486_2_pin8), .S1(hamming_syndrome_8_1_s1),
    .S2(hamming_syndrome_8_1_s2), .S4(hamming_syndrome_8_1_s4), .C(hamming_syndrome_8_1_c),
    .out_13(bitflip_8_1_out_13), .out_14(bitflip_8_1_out_14), .out_15(bitflip_8_1_out_15),
    .out_16(bitflip_8_1_out_16), .out_17(bitflip_8_1_out_17), .out_18(bitflip_8_1_out_18),
    .out_19(bitflip_8_1_out_19), .out_20(bitflip_8_1_out_20));
  Hamming_Syndrome_8 hamming_syndrome_8_1 (
    .R1(n7486_1_pin11), .R2(n7486_1_pin8), .R3(n7486_1_pin3), .R4(n7486_1_pin6), .R5(n7486_2_pin3),
    .R6(n7486_2_pin6), .R7(n7486_2_pin11), .R8(n7486_2_pin8), .S1(hamming_syndrome_8_1_s1),
    .S2(hamming_syndrome_8_1_s2), .S4(hamming_syndrome_8_1_s4), .C(hamming_syndrome_8_1_c));
  Data_Extract_4 data_extract_4_1 (
    .in_1(bitflip_8_1_out_13), .in_2(bitflip_8_1_out_14), .in_3(bitflip_8_1_out_15),
    .in_4(bitflip_8_1_out_16), .in_5(bitflip_8_1_out_17), .in_6(bitflip_8_1_out_18),
    .in_7(bitflip_8_1_out_19), .in_8(bitflip_8_1_out_20), .out_9(data_extract_4_1_out_9),
    .out_10(data_extract_4_1_out_10), .out_11(data_extract_4_1_out_11), .out_12(data_extract_4_1_out_12));
  LED led_1 (.in(data_extract_4_1_out_9));
  LED led_2 (.in(data_extract_4_1_out_10));
  LED led_3 (.in(data_extract_4_1_out_11));
  LED led_4 (.in(data_extract_4_1_out_12));
  SECDED_Classify secded_classify_1 (
    .S1(hamming_syndrome_8_1_s1), .S2(hamming_syndrome_8_1_s2), .S4(hamming_syndrome_8_1_s4),
    .C(hamming_syndrome_8_1_c), .noErr(out_13), .singleErr(out_14), .doubleErr(out_15));

  // Notes on the sheet:
  //   I1
  //   I2
  //   I3
  //   I4
  //   I5
  //   I6
  //   I7
  //   I8
endmodule

module Mem_Cell_8 (
  input  D_in1,
  input  D_in2,
  input  D_in3,
  input  D_in4,
  input  D_in5,
  input  D_in6,
  input  D_in7,
  input  D_in8,
  input  Clk,
  input  WriteEn,
  output Q1,
  output Q2,
  output Q3,
  output Q4,
  output Q5,
  output Q6,
  output Q7,
  output Q8
);

  wire n74157_1_pin4, n74157_1_pin7, n74157_1_pin9, n74157_1_pin12, n74157_2_pin4, n74157_2_pin7,
       n74157_2_pin9, n74157_2_pin12;

  D_Flip_Flop d_ff_1 (.D(n74157_1_pin4), .clk(Clk), .Q(Q1));  // open: Qn, preset, reset
  D_Flip_Flop d_ff_2 (.D(n74157_1_pin7), .clk(Clk), .Q(Q2));  // open: Qn, preset, reset
  D_Flip_Flop d_ff_3 (.D(n74157_1_pin9), .clk(Clk), .Q(Q3));  // open: Qn, preset, reset
  D_Flip_Flop d_ff_4 (.D(n74157_1_pin12), .clk(Clk), .Q(Q4));  // open: Qn, preset, reset
  D_Flip_Flop d_ff_5 (.D(n74157_2_pin4), .clk(Clk), .Q(Q5));  // open: Qn, preset, reset
  D_Flip_Flop d_ff_6 (.D(n74157_2_pin7), .clk(Clk), .Q(Q6));  // open: Qn, preset, reset
  D_Flip_Flop d_ff_7 (.D(n74157_2_pin12), .clk(Clk), .Q(Q7));  // open: Qn, preset, reset
  D_Flip_Flop d_ff_8 (.D(n74157_2_pin9), .clk(Clk), .Q(Q8));  // open: Qn, preset, reset
  _74157 #(.ShowInternalStructure("true")) u_74157_1 (
    .pin1(WriteEn), .pin2(Q1), .pin3(D_in1), .pin4(n74157_1_pin4), .pin5(Q2), .pin6(D_in2),
    .pin7(n74157_1_pin7), .pin14(Q4), .pin13(D_in4), .pin12(n74157_1_pin12), .pin11(Q3), .pin10(D_in3),
    .pin9(n74157_1_pin9));  // open: pin15
  _74157 #(.ShowInternalStructure("true")) u_74157_2 (
    .pin1(WriteEn), .pin2(Q5), .pin3(D_in5), .pin4(n74157_2_pin4), .pin5(Q6), .pin6(D_in6),
    .pin7(n74157_2_pin7), .pin14(Q7), .pin13(D_in7), .pin12(n74157_2_pin12), .pin11(Q8), .pin10(D_in8),
    .pin9(n74157_2_pin9));  // open: pin15
endmodule

module Step4_Test (
  input  D1,
  input  D2,
  input  D3,
  input  D4,
  input  Clk,
  input  WriteEn
);

  wire bitflip_8_1_out_13, bitflip_8_1_out_14, bitflip_8_1_out_15, bitflip_8_1_out_16, bitflip_8_1_out_17,
       bitflip_8_1_out_18, bitflip_8_1_out_19, bitflip_8_1_out_20, data_extract_4_1_out_9,
       data_extract_4_1_out_10, data_extract_4_1_out_11, data_extract_4_1_out_12, hamming_encode_4to8_1_r1,
       hamming_encode_4to8_1_r2, hamming_encode_4to8_1_r3, hamming_encode_4to8_1_r4,
       hamming_encode_4to8_1_r5, hamming_encode_4to8_1_r6, hamming_encode_4to8_1_r7,
       hamming_encode_4to8_1_r8, hamming_syndrome_8_1_c, hamming_syndrome_8_1_s1, hamming_syndrome_8_1_s2,
       hamming_syndrome_8_1_s4, mem_cell_8_1_q1, mem_cell_8_1_q2, mem_cell_8_1_q3, mem_cell_8_1_q4,
       mem_cell_8_1_q5, mem_cell_8_1_q6, mem_cell_8_1_q7, mem_cell_8_1_q8;

  Hamming_Encode_4to8 hamming_encode_4to8_1 (
    .D1(D1), .D2(D2), .D3(D3), .D4(D4), .R1(hamming_encode_4to8_1_r1), .R2(hamming_encode_4to8_1_r2),
    .R3(hamming_encode_4to8_1_r3), .R4(hamming_encode_4to8_1_r4), .R5(hamming_encode_4to8_1_r5),
    .R6(hamming_encode_4to8_1_r6), .R7(hamming_encode_4to8_1_r7), .R8(hamming_encode_4to8_1_r8));
  Mem_Cell_8 mem_cell_8_1 (
    .D_in1(hamming_encode_4to8_1_r1), .D_in2(hamming_encode_4to8_1_r2), .D_in3(hamming_encode_4to8_1_r3),
    .D_in4(hamming_encode_4to8_1_r4), .D_in5(hamming_encode_4to8_1_r5), .D_in6(hamming_encode_4to8_1_r6),
    .D_in7(hamming_encode_4to8_1_r7), .D_in8(hamming_encode_4to8_1_r8), .Clk(Clk), .WriteEn(WriteEn),
    .Q1(mem_cell_8_1_q1), .Q2(mem_cell_8_1_q2), .Q3(mem_cell_8_1_q3), .Q4(mem_cell_8_1_q4),
    .Q5(mem_cell_8_1_q5), .Q6(mem_cell_8_1_q6), .Q7(mem_cell_8_1_q7), .Q8(mem_cell_8_1_q8));
  Hamming_Syndrome_8 hamming_syndrome_8_1 (
    .R1(mem_cell_8_1_q1), .R2(mem_cell_8_1_q2), .R3(mem_cell_8_1_q3), .R4(mem_cell_8_1_q4),
    .R5(mem_cell_8_1_q5), .R6(mem_cell_8_1_q6), .R7(mem_cell_8_1_q7), .R8(mem_cell_8_1_q8),
    .S1(hamming_syndrome_8_1_s1), .S2(hamming_syndrome_8_1_s2), .S4(hamming_syndrome_8_1_s4),
    .C(hamming_syndrome_8_1_c));
  BitFlip_8 bitflip_8_1 (
    .R1(mem_cell_8_1_q1), .R2(mem_cell_8_1_q2), .R3(mem_cell_8_1_q3), .R4(mem_cell_8_1_q4),
    .R5(mem_cell_8_1_q5), .R6(mem_cell_8_1_q6), .R7(mem_cell_8_1_q7), .R8(mem_cell_8_1_q8),
    .S1(hamming_syndrome_8_1_s1), .S2(hamming_syndrome_8_1_s2), .S4(hamming_syndrome_8_1_s4),
    .C(hamming_syndrome_8_1_c), .out_13(bitflip_8_1_out_13), .out_14(bitflip_8_1_out_14),
    .out_15(bitflip_8_1_out_15), .out_16(bitflip_8_1_out_16), .out_17(bitflip_8_1_out_17),
    .out_18(bitflip_8_1_out_18), .out_19(bitflip_8_1_out_19), .out_20(bitflip_8_1_out_20));
  LED led_1 (.in(data_extract_4_1_out_9));
  Data_Extract_4 data_extract_4_1 (
    .in_1(bitflip_8_1_out_13), .in_2(bitflip_8_1_out_14), .in_3(bitflip_8_1_out_15),
    .in_4(bitflip_8_1_out_16), .in_5(bitflip_8_1_out_17), .in_6(bitflip_8_1_out_18),
    .in_7(bitflip_8_1_out_19), .in_8(bitflip_8_1_out_20), .out_9(data_extract_4_1_out_9),
    .out_10(data_extract_4_1_out_10), .out_11(data_extract_4_1_out_11), .out_12(data_extract_4_1_out_12));
  LED led_2 (.in(data_extract_4_1_out_10));
  LED led_3 (.in(data_extract_4_1_out_11));
  LED led_4 (.in(data_extract_4_1_out_12));
endmodule

module Error_Inject_8 (
  input  R1,
  input  R2,
  input  R3,
  input  R4,
  input  R5,
  input  R6,
  input  R7,
  input  R8,
  input  InjectEn,
  input  InjectPos0,
  input  InjectPos1,
  input  InjectPos2,
  output out_13,
  output out_14,
  output out_15,
  output out_16,
  output out_17,
  output out_18,
  output out_19,
  output out_20
);

  wire and_1_out, and_2_out, and_3_out, and_4_out, and_5_out, and_6_out, and_7_out, and_8_out, n74138_1_pin4,
       n74138_1_pin5, n74138_1_pin6, n74138_1_pin7, n74138_1_pin9, n74138_1_pin10, n74138_1_pin11,
       n74138_1_pin12, n74138_1_pin13, n74138_1_pin14, n74138_1_pin15, not_1_out, not_2_out, not_3_out,
       not_4_out, not_5_out, not_6_out, not_7_out, not_8_out;

  not not_1 (not_1_out, n74138_1_pin15);
  not not_2 (not_2_out, n74138_1_pin14);
  _74138 #(.ShowInternalStructure("true")) u_74138_1 (
    .pin1(InjectPos0), .pin2(InjectPos1), .pin3(InjectPos2), .pin4(n74138_1_pin4), .pin5(n74138_1_pin5),
    .pin6(n74138_1_pin6), .pin7(n74138_1_pin7), .pin15(n74138_1_pin15), .pin14(n74138_1_pin14),
    .pin13(n74138_1_pin13), .pin12(n74138_1_pin12), .pin11(n74138_1_pin11), .pin10(n74138_1_pin10),
    .pin9(n74138_1_pin9));
  not not_3 (not_3_out, n74138_1_pin13);
  not not_4 (not_4_out, n74138_1_pin12);
  not not_5 (not_5_out, n74138_1_pin11);
  not not_6 (not_6_out, n74138_1_pin10);
  not not_7 (not_7_out, n74138_1_pin7);
  not not_8 (not_8_out, n74138_1_pin9);
  and and_1 (and_1_out, InjectEn, not_1_out);
  and and_2 (and_2_out, InjectEn, not_2_out);
  and and_3 (and_3_out, InjectEn, not_3_out);
  and and_4 (and_4_out, InjectEn, not_4_out);
  and and_5 (and_5_out, InjectEn, not_5_out);
  and and_6 (and_6_out, InjectEn, not_6_out);
  and and_7 (and_7_out, InjectEn, not_8_out);
  and and_8 (and_8_out, InjectEn, not_7_out);
  xor xor_1 (out_13, R1, and_1_out);
  xor xor_2 (out_14, R2, and_2_out);
  xor xor_3 (out_15, R3, and_3_out);
  xor xor_4 (out_16, R4, and_4_out);
  xor xor_5 (out_17, R5, and_5_out);
  xor xor_6 (out_18, R6, and_6_out);
  xor xor_7 (out_19, R7, and_7_out);
  xor xor_8 (out_20, R8, and_8_out);
  // also tied to GND on the sheet: {n74138_1_pin4, n74138_1_pin5}
  // also tied to VCC on the sheet: n74138_1_pin6

  // Other names for the same wires on the sheet: i = InjectEn
endmodule

module Step5_Test (
  input  D1,
  input  D2,
  input  D3,
  input  D4,
  input  Clk,
  input  WriteEn,
  input  InjectEn,
  input  InjectPos0,
  input  InjectPos1,
  input  InjectPos2
);

  wire bitflip_8_1_out_13, bitflip_8_1_out_14, bitflip_8_1_out_15, bitflip_8_1_out_16, bitflip_8_1_out_17,
       bitflip_8_1_out_18, bitflip_8_1_out_19, bitflip_8_1_out_20, data_extract_4_1_out_9,
       data_extract_4_1_out_10, data_extract_4_1_out_11, data_extract_4_1_out_12, error_inject_8_1_out_13,
       error_inject_8_1_out_14, error_inject_8_1_out_15, error_inject_8_1_out_16, error_inject_8_1_out_17,
       error_inject_8_1_out_18, error_inject_8_1_out_19, error_inject_8_1_out_20, hamming_encode_4to8_1_r1,
       hamming_encode_4to8_1_r2, hamming_encode_4to8_1_r3, hamming_encode_4to8_1_r4,
       hamming_encode_4to8_1_r5, hamming_encode_4to8_1_r6, hamming_encode_4to8_1_r7,
       hamming_encode_4to8_1_r8, hamming_syndrome_8_1_c, hamming_syndrome_8_1_s1, hamming_syndrome_8_1_s2,
       hamming_syndrome_8_1_s4, mem_cell_8_1_q1, mem_cell_8_1_q2, mem_cell_8_1_q3, mem_cell_8_1_q4,
       mem_cell_8_1_q5, mem_cell_8_1_q6, mem_cell_8_1_q7, mem_cell_8_1_q8;

  Hamming_Encode_4to8 hamming_encode_4to8_1 (
    .D1(D1), .D2(D2), .D3(D3), .D4(D4), .R1(hamming_encode_4to8_1_r1), .R2(hamming_encode_4to8_1_r2),
    .R3(hamming_encode_4to8_1_r3), .R4(hamming_encode_4to8_1_r4), .R5(hamming_encode_4to8_1_r5),
    .R6(hamming_encode_4to8_1_r6), .R7(hamming_encode_4to8_1_r7), .R8(hamming_encode_4to8_1_r8));
  Mem_Cell_8 mem_cell_8_1 (
    .D_in1(hamming_encode_4to8_1_r1), .D_in2(hamming_encode_4to8_1_r2), .D_in3(hamming_encode_4to8_1_r3),
    .D_in4(hamming_encode_4to8_1_r4), .D_in5(hamming_encode_4to8_1_r5), .D_in6(hamming_encode_4to8_1_r6),
    .D_in7(hamming_encode_4to8_1_r7), .D_in8(hamming_encode_4to8_1_r8), .Clk(Clk), .WriteEn(WriteEn),
    .Q1(mem_cell_8_1_q1), .Q2(mem_cell_8_1_q2), .Q3(mem_cell_8_1_q3), .Q4(mem_cell_8_1_q4),
    .Q5(mem_cell_8_1_q5), .Q6(mem_cell_8_1_q6), .Q7(mem_cell_8_1_q7), .Q8(mem_cell_8_1_q8));
  Error_Inject_8 error_inject_8_1 (
    .R1(mem_cell_8_1_q1), .R2(mem_cell_8_1_q2), .R3(mem_cell_8_1_q3), .R4(mem_cell_8_1_q4),
    .R5(mem_cell_8_1_q5), .R6(mem_cell_8_1_q6), .R7(mem_cell_8_1_q7), .R8(mem_cell_8_1_q8),
    .InjectEn(InjectEn), .InjectPos0(InjectPos0), .InjectPos1(InjectPos1), .InjectPos2(InjectPos2),
    .out_13(error_inject_8_1_out_13), .out_14(error_inject_8_1_out_14), .out_15(error_inject_8_1_out_15),
    .out_16(error_inject_8_1_out_16), .out_17(error_inject_8_1_out_17), .out_18(error_inject_8_1_out_18),
    .out_19(error_inject_8_1_out_19), .out_20(error_inject_8_1_out_20));
  Hamming_Syndrome_8 hamming_syndrome_8_1 (
    .R1(error_inject_8_1_out_13), .R2(error_inject_8_1_out_14), .R3(error_inject_8_1_out_15),
    .R4(error_inject_8_1_out_16), .R5(error_inject_8_1_out_17), .R6(error_inject_8_1_out_18),
    .R7(error_inject_8_1_out_19), .R8(error_inject_8_1_out_20), .S1(hamming_syndrome_8_1_s1),
    .S2(hamming_syndrome_8_1_s2), .S4(hamming_syndrome_8_1_s4), .C(hamming_syndrome_8_1_c));
  BitFlip_8 bitflip_8_1 (
    .R1(error_inject_8_1_out_13), .R2(error_inject_8_1_out_14), .R3(error_inject_8_1_out_15),
    .R4(error_inject_8_1_out_16), .R5(error_inject_8_1_out_17), .R6(error_inject_8_1_out_18),
    .R7(error_inject_8_1_out_19), .R8(error_inject_8_1_out_20), .S1(hamming_syndrome_8_1_s1),
    .S2(hamming_syndrome_8_1_s2), .S4(hamming_syndrome_8_1_s4), .C(hamming_syndrome_8_1_c),
    .out_13(bitflip_8_1_out_13), .out_14(bitflip_8_1_out_14), .out_15(bitflip_8_1_out_15),
    .out_16(bitflip_8_1_out_16), .out_17(bitflip_8_1_out_17), .out_18(bitflip_8_1_out_18),
    .out_19(bitflip_8_1_out_19), .out_20(bitflip_8_1_out_20));
  LED led_1 (.in(data_extract_4_1_out_9));
  Data_Extract_4 data_extract_4_1 (
    .in_1(bitflip_8_1_out_13), .in_2(bitflip_8_1_out_14), .in_3(bitflip_8_1_out_15),
    .in_4(bitflip_8_1_out_16), .in_5(bitflip_8_1_out_17), .in_6(bitflip_8_1_out_18),
    .in_7(bitflip_8_1_out_19), .in_8(bitflip_8_1_out_20), .out_9(data_extract_4_1_out_9),
    .out_10(data_extract_4_1_out_10), .out_11(data_extract_4_1_out_11), .out_12(data_extract_4_1_out_12));
  LED led_2 (.in(data_extract_4_1_out_10));
  LED led_3 (.in(data_extract_4_1_out_11));
  LED led_4 (.in(data_extract_4_1_out_12));
endmodule

module Diagnostics (
  input  Reset,
  input  Clk,
  input  Read,
  input  noErr,
  input  singleErr,
  input  DoubleErr
);

  wire and_1_out, and_2_out, and_3_out, not_1_out;
  wire [3:0] DetectCounter_q, FixCounter_q, ReadCounter_q, UncorrectableCounter_q;

  not not_1 (not_1_out, noErr);
  and and_1 (and_1_out, Read, singleErr);
  and and_2 (and_2_out, not_1_out, Read);
  and and_3 (and_3_out, DoubleErr, Read);
  Counter #(.max('hf), .width(4)) ReadCounter (
    .clr(Reset), .load(1'b0), .up(1'b1), .count(Read), .clk(Clk), .Q(ReadCounter_q));  // open: D, carry
  Counter #(.max('hf), .width(4)) DetectCounter (
    .clr(Reset), .load(1'b0), .up(1'b1), .count(and_2_out), .clk(Clk), .Q(DetectCounter_q));  // open: D, carry
  Counter #(.max('hf), .width(4)) FixCounter (
    .clr(Reset), .load(1'b0), .up(1'b1), .count(and_1_out), .clk(Clk), .Q(FixCounter_q));  // open: D, carry
  Counter #(.max('hf), .width(4)) UncorrectableCounter (
    .clr(Reset), .load(1'b0), .up(1'b1), .count(and_3_out), .clk(Clk), .Q(UncorrectableCounter_q));  // open: D, carry
  Hex_Digit_Display hex_digit_display_1 (.value(ReadCounter_q));  // open: dp
  Hex_Digit_Display hex_digit_display_2 (.value(DetectCounter_q));  // open: dp
  Hex_Digit_Display hex_digit_display_3 (.value(FixCounter_q));  // open: dp
  Hex_Digit_Display hex_digit_display_4 (.value(UncorrectableCounter_q));  // open: dp

  // Notes on the sheet:
  //   Total Number of Reads
  //   Reads Where an Error was Detected
  //   Reads with a double error
  //   Reads where a single bit error was corrected
endmodule
